// Digital circuit Control Unit.dig as structural Verilog
module Control_Unit (
  input  [15:0] IR,
  input  CLK,
  input  S,
  input  R,
  input  I,
  input  IEN,
  input  FGI,
  input  FGO,
  input  E,
  input  [15:0] AC,
  input  [15:0] DR,
  input  C_OUT,
  output [6:0] x,
  output S_CLR,
  output I_LD,
  output I_D,
  output R_J,
  output R_K,
  output IEN_J,
  output IEN_K,
  output FGI_K,
  output FGO_K,
  output AR_LD,
  output AR_INR,
  output AR_CLR,
  output MEM_read,
  output MEM_write,
  output PC_LD,
  output PC_INCR,
  output PC_CLR,
  output DR_LD,
  output DR_INCR,
  output AC_LD,
  output AC_INCR,
  output AC_CLR,
  output [6:0] AL_OP,
  output OUTR_LD,
  output IR_LD,
  output TR_LD,
  output [15:0] T,
  output [7:0] D,
  output E_J,
  output E_K
);

  wire and_1_out, and_2_out, and_3_out, and_5_out, and_6_out, and_7_out, and_8_out, and_9_out, and_10_out,
       and_11_out, and_12_out, and_13_out, and_14_out, and_15_out, and_16_out, comparator_1_eq, E_J_t, E_K_t,
       I_t, multiplexer_2_out, not_1_out, not_2_out, not_3_out, not_4_out, not_5_out, not_6_out, not_7_out,
       or_3_out, or_4_out, or_6_out, PC_INCR_t, R_J_t, R_R, R_t, SC_CLR, SC_ovf, xor_1_out, xor_2_out;
  wire [1:0] priorityencoder_2_num, priorityencoder_3_num;
  wire [3:0] SC;
  wire [12:9] priorityencoder_1_num;

  PriorityEncoder #(.Selector_Bits(4)) priorityencoder_1 (
    .in0(IR[0]), .in1(IR[1]), .in2(IR[2]), .in3(IR[3]), .in4(IR[4]), .in5(IR[5]), .in6(IR[6]), .in7(IR[7]),
    .in8(IR[8]), .in9(IR[9]), .in10(IR[10]), .in11(IR[11]), .in12(1'b0), .in13(1'b0), .in14(1'b0),
    .in15(1'b0), .num(priorityencoder_1_num));  // open: any
  // Probe on priorityencoder_1_num
  ROM #(.AddrBits(13), .Bits(9)) ROM_2 (
    .A({priorityencoder_1_num, I_t, R_t, IR[14:12], SC}), .sel(1'b1),
    .D({SC_CLR, S_CLR, I_LD, R_J_t, R_K, IEN_J, IEN_K, FGI_K, FGO_K}));
  ROM #(.AddrBits(13), .Bits(16)) ROM_1 (
    .A({priorityencoder_1_num, I_t, R_t, IR[14:12], SC}), .sel(1'b1),
    .D({AR_LD, AR_INR, AR_CLR, MEM_read, MEM_write, PC_LD, PC_INCR_t, PC_CLR, DR_LD, DR_INCR, AC_LD, AC_INCR, AC_CLR, AL_OP[6:4]}));
  ROM #(.AddrBits(13), .Bits(16)) ROM_0 (
    .A({priorityencoder_1_num, I_t, R_t, IR[14:12], SC}), .sel(1'b1),
    .D({AL_OP[3:0], OUTR_LD, IR_LD, TR_LD, E_J_t, E_K_t, x}));
  or or_1 (I_t, I, I_D);
  or or_2 (R_t, R, R_R);
  or or_3 (or_3_out, not_1_out, SC_CLR);
  not not_1 (not_1_out, S);
  D_FF u_I (.D(IR[15]), .C(CLK), .Q(I_D));  // open: nQ
  Counter #(.Bits(4), .isProgramCounter("true")) u_SC (.en(1'b1), .C(CLK), .clr(or_3_out), .out(SC), .ovf(SC_ovf));
  or or_4 (or_4_out, FGI, FGO);
  and and_1 (and_1_out, IEN, or_4_out);
  and and_2 (and_2_out, not_2_out, not_3_out, not_4_out);
  not not_2 (not_2_out, T[2]);
  not not_3 (not_3_out, T[1]);
  not not_4 (not_4_out, T[0]);
  Decoder #(.Selector_Bits(3)) decoder_1 (
    .sel(IR[14:12]), .out_0(D[0]), .out_1(D[1]), .out_2(D[2]), .out_3(D[3]), .out_4(D[4]), .out_5(D[5]),
    .out_6(D[6]), .out_7(D[7]));
  Decoder #(.Selector_Bits(4)) decoder_2 (
    .sel(SC), .out_0(T[0]), .out_1(T[1]), .out_2(T[2]), .out_3(T[3]), .out_4(T[4]), .out_5(T[5]),
    .out_6(T[6]), .out_7(T[7]), .out_8(T[8]), .out_9(T[9]), .out_10(T[10]), .out_11(T[11]), .out_12(T[12]),
    .out_13(T[13]), .out_14(T[14]), .out_15(T[15]));
  LED led_1 (.in(SC_ovf));
  and and_3 (and_3_out, and_1_out, and_2_out);
  or or_5 (R_R, R_J_t, and_3_out);
  not not_5 (not_5_out, R);
  and and_4 (R_J, R_R, not_5_out);
  and and_5 (and_5_out, E_K_t, E_J_t);
  and and_6 (and_6_out, E_K_t, E_J_t);
  xor xor_1 (xor_1_out, AC[0], E);
  xor xor_2 (xor_2_out, AC[15], E);
  Comparator #(.Bits(16)) comparator_1 (.a(AC), .b({16{1'b0}}), .eq(comparator_1_eq));  // open: gt, lt
  and and_7 (and_7_out, E, and_5_out);
  and and_8 (and_8_out, comparator_1_eq, PC_INCR_t, IR[2]);
  not not_6 (not_6_out, E);
  and and_9 (and_9_out, IR[7], T[3]);
  and and_10 (and_10_out, IR[6], T[3]);
  not not_7 (not_7_out, AC[15]);
  and and_11 (and_11_out, not_7_out, PC_INCR_t, IR[4]);
  and and_12 (and_12_out, AC[15], PC_INCR_t, IR[3]);
  and and_13 (and_13_out, not_6_out, PC_INCR_t, IR[1]);
  Multiplexer #(.Selector_Bits(2)) multiplexer_1 (
    .sel(priorityencoder_2_num), .in_0(and_7_out), .in_1(and_6_out), .in_2(xor_1_out), .in_3(xor_2_out),
    .out(E_J));
  PriorityEncoder #(.Selector_Bits(2)) priorityencoder_2 (
    .in0(IR[10]), .in1(IR[8]), .in2(and_9_out), .in3(and_10_out), .num(priorityencoder_2_num));  // open: any
  PriorityEncoder #(.Selector_Bits(2)) priorityencoder_3 (
    .in0(IR[4]), .in1(IR[3]), .in2(IR[2]), .in3(IR[1]), .num(priorityencoder_3_num));  // open: any
  and and_14 (and_14_out, PC_INCR_t, T[1]);
  Multiplexer #(.Selector_Bits(2)) multiplexer_2 (
    .sel(priorityencoder_3_num), .in_0(and_11_out), .in_1(and_12_out), .in_2(and_8_out), .in_3(and_13_out),
    .out(multiplexer_2_out));
  or or_6 (or_6_out, and_14_out, multiplexer_2_out);
  and and_15 (and_15_out, FGI, PC_INCR_t, IR[9], T[3]);
  and and_16 (and_16_out, FGO, PC_INCR_t, IR[8], T[3]);
  or or_7 (PC_INCR, or_6_out, and_15_out, and_16_out);

  assign E_K = E_J;

  // Other names for the same wires on the sheet: AC_0 = AC[0]; AC_t[15:0] = AC; AC_15 = AC[15]; D_0 = D[0];
  //   D_1 = D[1]; D_2 = D[2]; D_3 = D[3]; D_4 = D[4]; D_5 = D[5]; D_6 = D[6]; D_7 = D[7]; B_0 = IR[0]; B_1 = IR[1];
  //   B_2 = IR[2]; B_3 = IR[3]; B_4 = IR[4]; B_5 = IR[5]; B_6 = IR[6]; B_7 = IR[7]; B_8 = IR[8]; B_9 = IR[9];
  //   B_10 = IR[10]; B_11 = IR[11]; D_t[2:0] = IR[14:12]; R_INPUT = R; T_0 = T[0]; T_1 = T[1]; T_2 = T[2]; T_3 = T[3];
  //   T_4 = T[4]; T_5 = T[5]; T_6 = T[6]; T_7 = T[7]; T_8 = T[8]; T_9 = T[9]; T_10 = T[10]; T_11 = T[11];
  //   T_12 = T[12]; T_13 = T[13]; T_14 = T[14]; T_15 = T[15]

  // Notes on the sheet:
  //   IR: default 62464
  //   CLK: Hz: 5
  //   S: default 1
  //   I: default 1
  //   contents of ROM_2 (hex, n*v repeats v):
  //   0,0,40,0,0,100,12*0,40,15*0,40,15*0,40,15*0,40,15*0,40,15*0,40
  //   ,15*0,40,180,142*0,40,0,0,100,12*0,40,15*0,40,15*0,40,15*0,40
  //   ,15*0,40,15*0,40,15*0,40,143*0,40,0,0,100,12*0,40,15*0,40,15*0
  //   ,40,15*0,40,15*0,40,15*0,40,15*0,40,100,142*0,40,0,0,100,12*0
  //   ,40,15*0,40,15*0,40,15*0,40,15*0,40,15*0,40,15*0,40,143*0,40,0,0
  //   ,100,12*0,40,15*0,40,15*0,40,15*0,40,15*0,40,15*0,40,15*0,40,100
  //   ,142*0,40,0,0,100,12*0,40,15*0,40,15*0,40,15*0,40,15*0,40,15*0
  //   ,40,15*0,40,143*0,40,0,0,100,12*0,40,15*0,40,15*0,40,15*0,40,15*0
  //   ,40,15*0,40,15*0,40,100,142*0,40,0,0,100,12*0,40,15*0,40,15*0
  //   ,40,15*0,40,15*0,40,15*0,40,15*0,40,143*0,40,0,0,100,12*0,40,15*0
  //   ,40,15*0,40,15*0,40,15*0,40,15*0,40,15*0,40,100,142*0,40,0,0,100
  //   ,12*0,40,15*0,40,15*0,40,15*0,40,15*0,40,15*0,40,15*0,40,143*0
  //   ,40,0,0,100,12*0,40,15*0,40,15*0,40,15*0,40,15*0,40,15*0,40,15*0
  //   ,40,100,142*0,40,0,0,100,12*0,40,15*0,40,15*0,40,15*0,40,15*0
  //   ,40,15*0,40,15*0,40,143*0,40,0,0,100,12*0,40,15*0,40,15*0,40,15*0
  //   ,40,15*0,40,15*0,40,15*0,40,100,142*0,40,0,0,100,12*0,40,15*0
  //   ,40,15*0,40,15*0,40,15*0,40,15*0,40,15*0,40,10c,142*0,40,0,0,100
  //   ,12*0,40,15*0,40,15*0,40,15*0,40,15*0,40,15*0,40,15*0,40,100,142*0
  //   ,40,0,0,100,12*0,40,15*0,40,15*0,40,15*0,40,15*0,40,15*0,40,15*0
  //   ,40,10c,142*0,40,0,0,100,12*0,40,15*0,40,15*0,40,15*0,40,15*0
  //   ,40,15*0,40,15*0,40,100,142*0,40,0,0,100,12*0,40,15*0,40,15*0
  //   ,40,15*0,40,15*0,40,15*0,40,15*0,40,100,142*0,40,0,0,100,12*0
  //   ,40,15*0,40,15*0,40,15*0,40,15*0,40,15*0,40,15*0,40,100,142*0
  //   ,40,0,0,100,12*0,40,15*0,40,15*0,40,15*0,40,15*0,40,15*0,40,15*0
  //   ,40,100,142*0,40,0,0,100,12*0,40,15*0,40,15*0,40,15*0,40,15*0
  //   ,40,15*0,40,15*0,40,100,142*0,40,0,0,100,12*0,40,15*0,40,15*0
  //   ,40,15*0,40,15*0,40,15*0,40,15*0,40,101,142*0,40,0,0,100,12*0
  //   ,40,15*0,40,15*0,40,15*0,40,15*0,40,15*0,40,15*0,40,100,142*0
  //   ,40,0,0,100,12*0,40,15*0,40,15*0,40,15*0,40,15*0,40,15*0,40,15*0
  //   ,40,102,142*0,40,0,0,100,12*0,40,15*0,40,15*0,40,15*0,40,15*0
  //   ,40,15*0,40,15*0,40,143*0,40,0,0,100,12*0,40,15*0,40,15*0,40,15*0
  //   ,40,15*0,40,15*0,40,15*0,40,143*0,40,0,0,100,12*0,40,15*0,40,15*0
  //   ,40,15*0,40,15*0,40,15*0,40,15*0,40,143*0,40,0,0,100,12*0,40,15*0
  //   ,40,15*0,40,15*0,40,15*0,40,15*0,40,15*0,40,143*0,40,0,0,100,12*0
  //   ,40,15*0,40,15*0,40,15*0,40,15*0,40,15*0,40,15*0,40,143*0,40,0,0
  //   ,100,12*0,40,15*0,40,15*0,40,15*0,40,15*0,40,15*0,40,15*0,40,143*0
  //   ,40,0,0,100,12*0,40,15*0,40,15*0,40,15*0,40,15*0,40,15*0,40,15*0
  //   ,40,143*0,40,0,0,100,12*0,40,15*0,40,15*0,40,15*0,40,15*0,40,15*0
  //   ,40,15*0,40
  //   contents of ROM_1 (hex, n*v repeats v):
  //   8000,1200,8000,0,1080,20,10*0,8000,1200,8000,13*0,8000,1200,8000
  //   ,13*0,8000,1200,8000,13*0,8000,1200,8000,13*0,8000,1200,8000,13*0
  //   ,8000,1200,8000,13*0,8000,1200,8000,141*0,8000,1200,8000,9000
  //   ,1080,20,10*0,8000,1200,8000,13*0,8000,1200,8000,13*0,8000,1200
  //   ,8000,13*0,8000,1200,8000,13*0,8000,1200,8000,13*0,8000,1200,8000
  //   ,13*0,8000,1200,8000,141*0,8000,1200,8000,0,1080,20,10*0,8000
  //   ,1200,8000,13*0,8000,1200,8000,13*0,8000,1200,8000,13*0,8000,1200
  //   ,8000,13*0,8000,1200,8000,13*0,8000,1200,8000,13*0,8000,1200,8000
  //   ,200,140*0,8000,1200,8000,9000,1080,20,10*0,8000,1200,8000,13*0
  //   ,8000,1200,8000,13*0,8000,1200,8000,13*0,8000,1200,8000,13*0,8000
  //   ,1200,8000,13*0,8000,1200,8000,13*0,8000,1200,8000,141*0,8000
  //   ,1200,8000,0,1080,20,10*0,8000,1200,8000,13*0,8000,1200,8000,13*0
  //   ,8000,1200,8000,13*0,8000,1200,8000,13*0,8000,1200,8000,13*0,8000
  //   ,1200,8000,13*0,8000,1200,8000,200,140*0,8000,1200,8000,9000,1080
  //   ,20,10*0,8000,1200,8000,13*0,8000,1200,8000,13*0,8000,1200,8000
  //   ,13*0,8000,1200,8000,13*0,8000,1200,8000,13*0,8000,1200,8000,13*0
  //   ,8000,1200,8000,141*0,8000,1200,8000,0,1080,20,10*0,8000,1200
  //   ,8000,13*0,8000,1200,8000,13*0,8000,1200,8000,13*0,8000,1200,8000
  //   ,13*0,8000,1200,8000,13*0,8000,1200,8000,13*0,8000,1200,8000,200
  //   ,140*0,8000,1200,8000,9000,1080,20,10*0,8000,1200,8000,13*0,8000
  //   ,1200,8000,13*0,8000,1200,8000,13*0,8000,1200,8000,13*0,8000,1200
  //   ,8000,13*0,8000,1200,8000,13*0,8000,1200,8000,141*0,8000,1200
  //   ,8000,0,1080,20,10*0,8000,1200,8000,13*0,8000,1200,8000,13*0,8000
  //   ,1200,8000,13*0,8000,1200,8000,13*0,8000,1200,8000,13*0,8000,1200
  //   ,8000,13*0,8000,1200,8000,200,140*0,8000,1200,8000,9000,1080,20
  //   ,10*0,8000,1200,8000,13*0,8000,1200,8000,13*0,8000,1200,8000,13*0
  //   ,8000,1200,8000,13*0,8000,1200,8000,13*0,8000,1200,8000,13*0,8000
  //   ,1200,8000,141*0,8000,1200,8000,0,1080,20,10*0,8000,1200,8000
  //   ,13*0,8000,1200,8000,13*0,8000,1200,8000,13*0,8000,1200,8000,13*0
  //   ,8000,1200,8000,13*0,8000,1200,8000,13*0,8000,1200,8000,10,140*0
  //   ,8000,1200,8000,9000,1080,20,10*0,8000,1200,8000,13*0,8000,1200
  //   ,8000,13*0,8000,1200,8000,13*0,8000,1200,8000,13*0,8000,1200,8000
  //   ,13*0,8000,1200,8000,13*0,8000,1200,8000,141*0,8000,1200,8000
  //   ,0,1080,20,10*0,8000,1200,8000,13*0,8000,1200,8000,13*0,8000,1200
  //   ,8000,13*0,8000,1200,8000,13*0,8000,1200,8000,13*0,8000,1200,8000
  //   ,13*0,8000,1200,8000,24,140*0,8000,1200,8000,9000,1080,20,10*0
  //   ,8000,1200,8000,13*0,8000,1200,8000,13*0,8000,1200,8000,13*0,8000
  //   ,1200,8000,13*0,8000,1200,8000,13*0,8000,1200,8000,13*0,8000,1200
  //   ,8000,141*0,8000,1200,8000,0,1080,20,10*0,8000,1200,8000,13*0
  //   ,8000,1200,8000,13*0,8000,1200,8000,13*0,8000,1200,8000,13*0,8000
  //   ,1200,8000,13*0,8000,1200,8000,13*0,8000,1200,8000,22,140*0,8000
  //   ,1200,8000,9000,1080,20,10*0,8000,1200,8000,13*0,8000,1200,8000
  //   ,13*0,8000,1200,8000,13*0,8000,1200,8000,13*0,8000,1200,8000,13*0
  //   ,8000,1200,8000,13*0,8000,1200,8000,141*0,8000,1200,8000,0,1080
  //   ,20,10*0,8000,1200,8000,13*0,8000,1200,8000,13*0,8000,1200,8000
  //   ,13*0,8000,1200,8000,13*0,8000,1200,8000,13*0,8000,1200,8000,13*0
  //   ,8000,1200,8000,141*0,8000,1200,8000,9000,1080,20,10*0,8000,1200
  //   ,8000,13*0,8000,1200,8000,13*0,8000,1200,8000,13*0,8000,1200,8000
  //   ,13*0,8000,1200,8000,13*0,8000,1200,8000,13*0,8000,1200,8000,200
  //   ,140*0,8000,1200,8000,0,1080,20,10*0,8000,1200,8000,13*0,8000
  //   ,1200,8000,13*0,8000,1200,8000,13*0,8000,1200,8000,13*0,8000,1200
  //   ,8000,13*0,8000,1200,8000,13*0,8000,1200,8000,21,140*0,8000,1200
  //   ,8000,9000,1080,20,10*0,8000,1200,8000,13*0,8000,1200,8000,13*0
  //   ,8000,1200,8000,13*0,8000,1200,8000,13*0,8000,1200,8000,13*0,8000
  //   ,1200,8000,13*0,8000,1200,8000,200,140*0,8000,1200,8000,0,1080
  //   ,20,10*0,8000,1200,8000,13*0,8000,1200,8000,13*0,8000,1200,8000
  //   ,13*0,8000,1200,8000,13*0,8000,1200,8000,13*0,8000,1200,8000,13*0
  //   ,8000,1200,8000,141*0,8000,1200,8000,9000,1080,20,10*0,8000,1200
  //   ,8000,13*0,8000,1200,8000,13*0,8000,1200,8000,13*0,8000,1200,8000
  //   ,13*0,8000,1200,8000,13*0,8000,1200,8000,13*0,8000,1200,8000,141*0
  //   ,8000,1200,8000,0,1080,20,10*0,8000,1200,8000,13*0,8000,1200,8000
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  //   contents of ROM_0 (hex, n*v repeats v):
  //   2,440,10,0,40,1000,10*0,2,440,10,13*0,2,440,10,13*0,2,440,10,13*0
  //   ,2,440,10,13*0,2,440,10,13*0,2,440,10,13*0,2,440,10,141*0,2,440
  //   ,10,40,40,1000,10*0,2,440,10,13*0,2,440,10,13*0,2,440,10,13*0
  //   ,2,440,10,13*0,2,440,10,13*0,2,440,10,13*0,2,440,10,141*0,2,440
  //   ,10,0,40,1000,10*0,2,440,10,13*0,2,440,10,13*0,2,440,10,13*0,2
  //   ,440,10,13*0,2,440,10,13*0,2,440,10,13*0,2,440,10,141*0,2,440
  //   ,10,40,40,1000,10*0,2,440,10,13*0,2,440,10,13*0,2,440,10,13*0
  //   ,2,440,10,13*0,2,440,10,13*0,2,440,10,13*0,2,440,10,141*0,2,440
  //   ,10,0,40,1000,10*0,2,440,10,13*0,2,440,10,13*0,2,440,10,13*0,2
  //   ,440,10,13*0,2,440,10,13*0,2,440,10,13*0,2,440,10,141*0,2,440
  //   ,10,40,40,1000,10*0,2,440,10,13*0,2,440,10,13*0,2,440,10,13*0
  //   ,2,440,10,13*0,2,440,10,13*0,2,440,10,13*0,2,440,10,141*0,2,440
  //   ,10,0,40,1000,10*0,2,440,10,13*0,2,440,10,13*0,2,440,10,13*0,2
  //   ,440,10,13*0,2,440,10,13*0,2,440,10,13*0,2,440,10,141*0,2,440
  //   ,10,40,40,1000,10*0,2,440,10,13*0,2,440,10,13*0,2,440,10,13*0
  //   ,2,440,10,13*0,2,440,10,13*0,2,440,10,13*0,2,440,10,141*0,2,440
  //   ,10,0,40,1000,10*0,2,440,10,13*0,2,440,10,13*0,2,440,10,13*0,2
  //   ,440,10,13*0,2,440,10,13*0,2,440,10,13*0,2,440,10,141*0,2,440
  //   ,10,40,40,1000,10*0,2,440,10,13*0,2,440,10,13*0,2,440,10,13*0
  //   ,2,440,10,13*0,2,440,10,13*0,2,440,10,13*0,2,440,10,141*0,2,440
  //   ,10,0,40,1000,10*0,2,440,10,13*0,2,440,10,13*0,2,440,10,13*0,2
  //   ,440,10,13*0,2,440,10,13*0,2,440,10,13*0,2,440,10,141*0,2,440
  //   ,10,40,40,1000,10*0,2,440,10,13*0,2,440,10,13*0,2,440,10,13*0
  //   ,2,440,10,13*0,2,440,10,13*0,2,440,10,13*0,2,440,10,141*0,2,440
  //   ,10,0,40,1000,10*0,2,440,10,13*0,2,440,10,13*0,2,440,10,13*0,2
  //   ,440,10,13*0,2,440,10,13*0,2,440,10,13*0,2,440,10,141*0,2,440
  //   ,10,40,40,1000,10*0,2,440,10,13*0,2,440,10,13*0,2,440,10,13*0
  //   ,2,440,10,13*0,2,440,10,13*0,2,440,10,13*0,2,440,10,141*0,2,440
  //   ,10,0,40,1000,10*0,2,440,10,13*0,2,440,10,13*0,2,440,10,13*0,2
  //   ,440,10,13*0,2,440,10,13*0,2,440,10,13*0,2,440,10,141*0,2,440
  //   ,10,40,40,1000,10*0,2,440,10,13*0,2,440,10,13*0,2,440,10,13*0
  //   ,2,440,10,13*0,2,440,10,13*0,2,440,10,13*0,2,440,10,141*0,2,440
  //   ,10,0,40,1000,10*0,2,440,10,13*0,2,440,10,13*0,2,440,10,13*0,2
  //   ,440,10,13*0,2,440,10,13*0,2,440,10,13*0,2,440,10,180,140*0,2
  //   ,440,10,40,40,1000,10*0,2,440,10,13*0,2,440,10,13*0,2,440,10,13*0
  //   ,2,440,10,13*0,2,440,10,13*0,2,440,10,13*0,2,440,10,141*0,2,440
  //   ,10,0,40,1000,10*0,2,440,10,13*0,2,440,10,13*0,2,440,10,13*0,2
  //   ,440,10,13*0,2,440,10,13*0,2,440,10,13*0,2,440,10,141*0,2,440
  //   ,10,40,40,1000,10*0,2,440,10,13*0,2,440,10,13*0,2,440,10,13*0
  //   ,2,440,10,13*0,2,440,10,13*0,2,440,10,13*0,2,440,10,141*0,2,440
  //   ,10,0,40,1000,10*0,2,440,10,13*0,2,440,10,13*0,2,440,10,13*0,2
  //   ,440,10,13*0,2,440,10,13*0,2,440,10,13*0,2,440,10,180,140*0,2
  //   ,440,10,40,40,1000,10*0,2,440,10,13*0,2,440,10,13*0,2,440,10,13*0
  //   ,2,440,10,13*0,2,440,10,13*0,2,440,10,13*0,2,440,10,808,140*0
  //   ,2,440,10,0,40,1000,10*0,2,440,10,13*0,2,440,10,13*0,2,440,10
  //   ,13*0,2,440,10,13*0,2,440,10,13*0,2,440,10,13*0,2,440,10,141*0
  //   ,2,440,10,40,40,1000,10*0,2,440,10,13*0,2,440,10,13*0,2,440,10
  //   ,13*0,2,440,10,13*0,2,440,10,13*0,2,440,10,13*0,2,440,10,8000
  //   ,140*0,2,440,10,0,40,1000,10*0,2,440,10,13*0,2,440,10,13*0,2,440
  //   ,10,13*0,2,440,10,13*0,2,440,10,13*0,2,440,10,13*0,2,440,10,141*0
  //   ,2,440,10,40,40,1000,10*0,2,440,10,13*0,2,440,10,13*0,2,440,10
  //   ,13*0,2,440,10,13*0,2,440,10,13*0,2,440,10,13*0,2,440,10,141*0
  //   ,2,440,10,0,40,1000,10*0,2,440,10,13*0,2,440,10,13*0,2,440,10
  //   ,13*0,2,440,10,13*0,2,440,10,13*0,2,440,10,13*0,2,440,10,141*0
  //   ,2,440,10,40,40,1000,10*0,2,440,10,13*0,2,440,10,13*0,2,440,10
  //   ,13*0,2,440,10,13*0,2,440,10,13*0,2,440,10,13*0,2,440,10,141*0
  //   ,2,440,10,0,40,1000,10*0,2,440,10,13*0,2,440,10,13*0,2,440,10
  //   ,13*0,2,440,10,13*0,2,440,10,13*0,2,440,10,13*0,2,440,10,141*0
  //   ,2,440,10,40,40,1000,10*0,2,440,10,13*0,2,440,10,13*0,2,440,10
  //   ,13*0,2,440,10,13*0,2,440,10,13*0,2,440,10,13*0,2,440,10,141*0
  //   ,2,440,10,0,40,1000,10*0,2,440,10,13*0,2,440,10,13*0,2,440,10
  //   ,13*0,2,440,10,13*0,2,440,10,13*0,2,440,10,13*0,2,440,10,141*0
  //   ,2,440,10,40,40,1000,10*0,2,440,10,13*0,2,440,10,13*0,2,440,10
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endmodule
